# Fritzing sketch Roomba_Wiring (saved by Fritzing 0.9.9b)

parts:
  U3 = DIN7 [part_number="Serial Port Mini DIN" package=din7]  # not connected
  Q1 = PNP-Transistor [part_number=2N3906 package="TO92 [THT]"]
  WeMos_D1_Mini1 = WeMos D1 Mini [part_number="D1 mini"]
  U5 = Buck Converter [package=odfn6]

nets:
  N1: Q1.E, WeMos_D1_Mini1.RX
  N2: Q1.C, WeMos_D1_Mini1.G, U5.ESP_-
  N3: WeMos_D1_Mini1.3V3, U5.Roomba_-

notes:
  PNP
  Transistor
  2N3906 (EBC)
  D1 mini
  Roomba
  OI Port
  Buck Converter
  14V -> 3,3V
  GND (Pin7)
  Vpwr (Pin2)
  3,3V
  BRC (Pin5)
  RXD (Pin3)
  TXD (Pin4)
  GND
